# Fritzing sketch LED Übung (saved by Fritzing 0.9.3b)
breadboards: 1

parts:
  Bauteil1 = Arduino Uno (Rev3) - ICSP
  R1 = Resistor [tolerance=±5% resistance=200 package=THT]
  R2 = Resistor [tolerance=±5% resistance=200 package=THT]
  LED1 = LED - 5mm [color="Red (633nm)" package="5 mm [THT]"]
  LED2 = LED - 5mm [color="Green (570nm)" package="5 mm [THT]"]

nets:
  N1: Bauteil1.GND, LED1.cathode, LED2.cathode
  N2: Bauteil1.D1/TX, R1.Pin_1
  N3: Bauteil1.D4, R2.Pin_0
  N4: R1.Pin_0, LED2.anode
  N5: R2.Pin_1, LED1.anode
