# Fritzing sketch Moisture (saved by Fritzing 0.9.3b)

parts:
  Bauteil1 = Arduino Ethernet Shield (Rev3)
  Bauteil2 = Soil Moisture Sensor

nets:
  N1: Bauteil1.A0, Bauteil2.SIG
  5V: Bauteil1.5V, Bauteil2.VCC
  GND: Bauteil1.GND, Bauteil2.GND
