# Fritzing sketch Photosensor (saved by Fritzing 0.9.3b)
breadboards: 1

parts:
  Bauteil1 = Arduino Uno (Rev3)
  R1 = PHOTOCELL [package=photocell-kit]
  R2 = Resistor [tolerance=±5% resistance=1k package=THT]
  LED1 = RGB LED (com. cathode, rgb) [package="5 mm [THT]"]
  R3 = Resistor [tolerance=±5% resistance=200 package=THT]
  R4 = Resistor [tolerance=±5% resistance=200 package=THT]
  R5 = Resistor [tolerance=±5% resistance=200 package=THT]

nets:
  N1: Bauteil1.A0, R1.P$1, R2.Pin_1
  N2: Bauteil1.D9_PWM, R3.Pin_0
  N3: Bauteil1.D10_PWM/SS, R4.Pin_0
  N4: Bauteil1.D11_PWM/MOSI, R5.Pin_0
  N5: Bauteil1.5V, R1.P$2
  N6: Bauteil1.GND, R2.Pin_0
  N7: LED1.red_anode, R5.Pin_1
  N8: LED1.green_anode, R4.Pin_1
  N9: LED1.blue_anode, R3.Pin_1
