# Fritzing sketch RGB LED (saved by Fritzing 0.9.3b)
breadboards: 1

parts:
  Bauteil1 = Arduino Uno (Rev3)
  LED1 = RGB LED (com. cathode, rbg) [package="5 mm [THT]"]
  R1 = Resistor [tolerance=±5% resistance=200 package=THT]
  R2 = Resistor [tolerance=±5% resistance=200 package=THT]
  R4 = Resistor [tolerance=±5% resistance=200 package=THT]
  S1 = Pushbutton [package="[THT]"]
  S2 = Pushbutton [package="[THT]"]

nets:
  N1: Bauteil1.D10_PWM/SS, R4.Pin_0
  N2: Bauteil1.D11_PWM/MOSI, S1.Pin_1, S1.Pin_2
  N3: Bauteil1.D3_PWM, S2.Pin_3, S2.Pin_4
  N4: Bauteil1.D5_PWM, R1.Pin_0
  N5: Bauteil1.D6_PWM, R2.Pin_0
  N6: Bauteil1.GND, LED1.common_cathode, S1.Pin_3, S1.Pin_4, S2.Pin_1, S2.Pin_2
  N7: LED1.red_anode, R4.Pin_1
  N8: LED1.blue_anode, R2.Pin_1
  N9: LED1.green_anode, R1.Pin_1
