# Fritzing sketch ReactionGame (saved by Fritzing 0.9.3b)
breadboards: 1

parts:
  Bauteil1 = Arduino Uno (Rev3)
  R1 = Resistor [tolerance=±5% resistance=200 package=THT]
  LED1 = LED - 5mm [color="Green (555nm)" package="5 mm [THT]"]
  S1 = Pushbutton [package="[SMD]"]
  R2 = Resistor [tolerance=±5% resistance=200 package=THT]
  LED2 = LED - 5mm [color="Red (633nm)" package="5 mm [THT]"]
  S3 = Pushbutton [package="[THT]"]

nets:
  N1: Bauteil1.D11_PWM/MOSI, S3.Pin_3, S3.Pin_4
  N2: Bauteil1.D13/SCK, R2.Pin_0
  N3: Bauteil1.D1/TX, R1.Pin_0
  N4: Bauteil1.D3_PWM, S1.Pin_1, S1.Pin_2
  N5: Bauteil1.GND, LED1.cathode, S1.Pin_3, S1.Pin_4, LED2.cathode, S3.Pin_1, S3.Pin_2
  N6: R1.Pin_1, LED1.anode
  N7: R2.Pin_1, LED2.anode
