# Fritzing sketch Temperature (saved by Fritzing 0.9.3b)
breadboards: 1

parts:
  Bauteil1 = Arduino Uno (Rev3)
  T1 = TMP36 Temperature Sensor [package="TO92 [THT]"]
  R1 = Resistor [tolerance=±5% resistance=200 package=THT]
  LED1 = LED - 5mm [color="Red (633nm)" package="5 mm [THT]"]
  R2 = Resistor [tolerance=±5% resistance=200 package=THT]
  LED2 = LED - 5mm [color="Green (555nm)" package="5 mm [THT]"]

nets:
  N1: Bauteil1.A2, T1.Vout
  GND: Bauteil1.GND, T1.GND, LED1.cathode, LED2.cathode
  N2: Bauteil1.D0/RX, R2.Pin_0
  N3: Bauteil1.D7, R1.Pin_0
  N4: Bauteil1.5V, T1.+Vs
  N5: R1.Pin_1, LED1.anode
  N6: R2.Pin_1, LED2.anode
