# Fritzing sketch Ultrasonic (saved by Fritzing 0.9.3b)
breadboards: 1

parts:
  Bauteil1 = Arduino Uno (Rev3)
  hc-sr1 = hc-sr04
  J1 = Piezo Speaker
  R1 = Resistor [tolerance=±5% resistance=200 package=THT]
  R2 = Resistor [tolerance=±5% resistance=200 package=THT]
  R3 = Resistor [tolerance=±5% resistance=200 package=THT]
  LED2 = LED - 5mm [color="Yellow (595nm)" package="5 mm [THT]"]
  LED3 = LED - 5mm [color="Green (570nm)" package="5 mm [THT]"]
  LED4 = LED - 5mm [color="Red (633nm)" package="5 mm [THT]"]

nets:
  N1: Bauteil1.D10_PWM/SS, R3.Pin_0
  N2: Bauteil1.D11_PWM/MOSI, R2.Pin_0
  N3: Bauteil1.D12/MISO, R1.Pin_0
  N4: Bauteil1.D5_PWM, J1.pin2
  N5: Bauteil1.D6_PWM, hc-sr1.Echo
  N6: Bauteil1.D7, hc-sr1.Trig
  5V: Bauteil1.5V, hc-sr1.VCC
  GND: Bauteil1.GND, hc-sr1.GND, J1.pin1, LED2.cathode, LED3.cathode, LED4.cathode
  N7: R1.Pin_1, LED4.anode
  N8: R2.Pin_1, LED2.anode
  N9: R3.Pin_1, LED3.anode
