# Fritzing sketch servo (saved by Fritzing 0.9.3b)
breadboards: 1

parts:
  Bauteil1 = Arduino Uno (Rev3)
  J1 = Basic Servo
  R1 = Rotary Potentiometer (Small) [maximum_resistance=100kΩ package=THT]

nets:
  N1: Bauteil1.A0, R1.wiper
  N2: Bauteil1.D8, J1.pulse
  GND: Bauteil1.GND, J1.gnd, R1.leg1
  5V: Bauteil1.5V, J1.vcc, R1.leg2
