# Fritzing sketch Infrared (saved by Fritzing 0.9.3b)
breadboards: 1

parts:
  Part1 = KY-022 Infrared Receiver Module [package="Breakout board"]
  Raspberry_Pi1 = Raspberry Pi B+
  LED1 = RGB LED (com. cathode, rgb) [package="5 mm [THT]"]
  R1 = Resistor [tolerance=±5% resistance=200 package=THT]
  R2 = Resistor [tolerance=±5% resistance=200 package=THT]
  R3 = Resistor [tolerance=±5% resistance=200 package=THT]

nets:
  N1: Part1.S, Raspberry_Pi1.GPIO12
  VIN: Part1.Vin, Raspberry_Pi1.3v3
  N2: Part1.-, Raspberry_Pi1.GND, LED1.common_cathode
  N3: Raspberry_Pi1.GPIO21, R3.Pin_0
  N4: Raspberry_Pi1.GPIO20, R2.Pin_0
  N5: Raspberry_Pi1.GPIO16, R1.Pin_0
  N6: LED1.red_anode, R1.Pin_1
  N7: LED1.green_anode, R2.Pin_1
  N8: LED1.blue_anode, R3.Pin_1

custom parts:
  KY-022 Infrared Receiver Module: Arduino IR receiver module KY-022, reacts to 38kHz infrared light.
