# Fritzing sketch LCD (saved by Fritzing 0.9.3b)
breadboards: 1

parts:
  U1 = LCD-16X2 [package=lcd-16x2]
  LCM1602_IIC1 = LCM1602 IIC [part_number="LCM1602 IIC" chip_label="LCM1602 IIC" package="DIP (Dual Inline) [THT]"]
  Raspberry_Pi1 = Raspberry Pi B+
  Part1 = KY-001 Temperature Sensor Module [package="Breakout board"]

nets:
  VSS: U1.VSS, LCM1602_IIC1.VSS
  VDD: U1.VDD, LCM1602_IIC1.VDD
  N1: U1.VO, LCM1602_IIC1.V0
  N2: U1.RS, LCM1602_IIC1.RS
  N3: U1.R_W, LCM1602_IIC1.RW
  N4: U1.E, LCM1602_IIC1.E
  N5: U1.DB0, LCM1602_IIC1.D0
  N6: U1.DB1, LCM1602_IIC1.D1
  N7: U1.DB2, LCM1602_IIC1.D2
  N8: U1.DB3, LCM1602_IIC1.D3
  N9: U1.DB4, LCM1602_IIC1.D4
  N10: U1.DB5, LCM1602_IIC1.D5
  N11: U1.DB6, LCM1602_IIC1.D6
  N12: U1.DB7, LCM1602_IIC1.D7
  N13: U1.A, LCM1602_IIC1.A
  N14: U1.K, LCM1602_IIC1.K
  GND: LCM1602_IIC1.GND, Raspberry_Pi1.GND, Part1.-
  VCC: LCM1602_IIC1.VCC, LCM1602_IIC1.SDA, LCM1602_IIC1.SCL, Raspberry_Pi1.3v3, Raspberry_Pi1.GPIO2, Raspberry_Pi1.GPIO3, Part1.Vin
  N15: LCM1602_IIC1.LED_A, LCM1602_IIC1.LED_B
  N16: Raspberry_Pi1.GPIO21, Part1.S

custom parts:
  LCM1602 IIC: I2C-Module to use a 1602 or 2004 LCD on with the wire.h libory Serial LCD Modul
  KY-001 Temperature Sensor Module: Arduino Temperature Sensor Module Keyes KY-001, Allows ambient temperature measurement using digital serial bus (DS18B20)
