# Fritzing sketch Line (saved by Fritzing 0.9.3b)
breadboards: 1

parts:
  Bauteil1 = KY-033 Tracing Black White Line Hunting Sensor Module For Arduino
  Raspberry_Pi1 = Raspberry Pi B+
  LED1 = RGB LED (com. cathode, rgb) [package="5 mm [THT]"]
  R1 = Resistor [tolerance=±5% resistance=200 package=THT]
  R2 = Resistor [tolerance=±5% resistance=200 package=THT]
  R3 = Resistor [tolerance=±5% resistance=200 package=THT]

nets:
  GND: Bauteil1.GND, Raspberry_Pi1.GND, LED1.common_cathode
  N1: Bauteil1.V+, Raspberry_Pi1.3v3
  N2: Bauteil1.S, Raspberry_Pi1.GPIO12
  N3: Raspberry_Pi1.GPIO21, R3.Pin_0
  N4: Raspberry_Pi1.GPIO20, R2.Pin_0
  N5: Raspberry_Pi1.GPIO16, R1.Pin_0
  N6: LED1.red_anode, R1.Pin_1
  N7: LED1.green_anode, R2.Pin_1
  N8: LED1.blue_anode, R3.Pin_1

custom parts:
  KY-033 Tracing Black White Line Hunting Sensor Module For Arduino: Tracing Black White Line Hunting Sensor Module For Arduino Description: This is KY-033 tracking sensor. The KY-033 measures the intensity of infrared radiation and delivers it as an analog output voltage. Features: Operating voltage: 2.5 - 12V(cannot over12V) working current: 18mA-20mA at 5V Enhanced accuracy Documents: http://www.vishay.com/docs/83760/tcrt5000.pdf
