# Fritzing sketch Temperatur (saved by Fritzing 0.9.3b)
breadboards: 1

parts:
  Raspberry_Pi1 = Raspberry Pi B+
  Part1 = KY-015 Temperature & Humidity Sensor Module [package="Breakout board"]
  Part2 = KY-002 Vibration Switch Module [package="Breakout board"]

nets:
  N1: Raspberry_Pi1.GND, Part1.-, Part2.-
  N2: Raspberry_Pi1.GPIO21, Part2.S
  N3: Raspberry_Pi1.GPIO20, Part1.S
  VIN: Raspberry_Pi1.5V, Part1.Vin, Part2.Vin

custom parts:
  KY-015 Temperature & Humidity Sensor Module: KY-015 temperature and humidity sensor module, provides a low-latency serial interface to measure humidity and temperature.
  KY-002 Vibration Switch Module: Arduino Vibration Switch Module KY-002 Keyes allows detection of shock and vibration.
